# Fritzing sketch ijn_main (saved by Fritzing 0.9.3b)
circuit board: 7.71328cm x 6.18248cm
breadboards: 1

parts:
  IchigoJam_T1 = IchigoJam T  # not connected
  J1 = female pin header, 14 pins [form="♀ (female)"]
  J2 = female pin header, 14 pins [form="♀ (female)"]
  J3 = female pin header, 5 pins [form="♀ (female)"]  # not connected
  J5 = female pin header, 6 pins [form="♀ (female)"]
  A2 = AE-DRV8835-S-1  # not connected
  J4 = female pin header, 6 pins [form="♀ (female)"]
  Power_plug1 = Power plug
  TRM2 = Terminal 2pin
  TRM3 = Terminal 2pin
  S1 = Akizuki slide switch IS-2235
  J34 = rounded female pin header, 1 pin [form="♀ (female rounded)"]
  J35 = rounded female pin header, 1 pin [form="♀ (female rounded)"]
  J36 = rounded female pin header, 1 pin [form="♀ (female rounded)"]
  J37 = rounded female pin header, 1 pin [form="♀ (female rounded)"]
  J38 = rounded female pin header, 1 pin [form="♀ (female rounded)"]
  J39 = rounded female pin header, 1 pin [form="♀ (female rounded)"]
  J40 = rounded female pin header, 1 pin [form="♀ (female rounded)"]  # not connected
  J41 = rounded female pin header, 1 pin [form="♀ (female rounded)"]
  J9 = rounded female pin header, 1 pin [form="♀ (female rounded)"]
  J8 = rounded female pin header, 1 pin [form="♀ (female rounded)"]  # not connected
  J7 = rounded female pin header, 1 pin [form="♀ (female rounded)"]
  J6 = rounded female pin header, 1 pin [form="♀ (female rounded)"]
  J10 = rounded female pin header, 1 pin [form="♀ (female rounded)"]
  J11 = rounded female pin header, 1 pin [form="♀ (female rounded)"]
  J12 = rounded female pin header, 1 pin [form="♀ (female rounded)"]
  J13 = rounded female pin header, 1 pin [form="♀ (female rounded)"]
  J14 = rounded female pin header, 1 pin [form="♀ (female rounded)"]
  J15 = rounded female pin header, 1 pin [form="♀ (female rounded)"]
  J16 = rounded female pin header, 1 pin [form="♀ (female rounded)"]
  J17 = rounded female pin header, 1 pin [form="♀ (female rounded)"]
  J18 = rounded female pin header, 1 pin [form="♀ (female rounded)"]
  J19 = rounded female pin header, 1 pin [form="♀ (female rounded)"]
  J20 = rounded female pin header, 1 pin [form="♀ (female rounded)"]
  J21 = rounded female pin header, 1 pin [form="♀ (female rounded)"]
  J22 = rounded female pin header, 1 pin [form="♀ (female rounded)"]
  J23 = rounded female pin header, 1 pin [form="♀ (female rounded)"]
  J24 = rounded female pin header, 1 pin [form="♀ (female rounded)"]
  J25 = rounded female pin header, 1 pin [form="♀ (female rounded)"]
  J26 = rounded female pin header, 1 pin [form="♀ (female rounded)"]
  J27 = rounded female pin header, 1 pin [form="♀ (female rounded)"]
  J28 = rounded female pin header, 1 pin [form="♀ (female rounded)"]
  J29 = rounded female pin header, 1 pin [form="♀ (female rounded)"]  # not connected
  J31 = rounded female pin header, 1 pin [form="♀ (female rounded)"]
  J30 = rounded female pin header, 1 pin [form="♀ (female rounded)"]
  J33 = rounded female pin header, 1 pin [form="♀ (female rounded)"]
  J32 = rounded female pin header, 1 pin [form="♀ (female rounded)"]  # not connected

nets (from the pcb view):
  N1: J1.pin7, J37.pin1, J41.pin1, J33.pin1
  N2: J1.pin8, J5.pin1, J34.pin1
  N3: J1.pin11, S1.pin4, J39.pin1
  N4: J1.pin12, J35.pin1
  N5: J1.pin13, J31.pin1
  N6: J1.pin14, J30.pin1
  N7: J2.pin3, J28.pin1
  N8: J2.pin4, J24.pin1
  N9: J2.pin5, J20.pin1
  N10: J2.pin7, J17.pin1, J19.pin1
  N11: J2.pin8, J4.pin1, Power_plug1.GND, J9.pin1, J10.pin1, J14.pin1, J18.pin1, J22.pin1, J26.pin1
  N12: J2.pin10, J5.pin4
  N13: J2.pin11, J5.pin3
  N14: J2.pin12, S1.pin1, J16.pin1
  N15: J2.pin13, J12.pin1
  N16: J2.pin14, J7.pin1
  N17: J5.pin5, S1.pin0
  N18: J5.pin6, S1.pin3
  N19: J4.pin2, TRM3.pin_1
  N20: J4.pin3, TRM3.pin_2
  N21: J4.pin4, TRM2.pin_1
  N22: J4.pin5, TRM2.pin_2
  N23: J4.pin6, Power_plug1.VCC
  N24: J36.pin1, J38.pin1
  N25: J6.pin1, J11.pin1
  N26: J13.pin1, J15.pin1
  N27: J21.pin1, J23.pin1
  N28: J25.pin1, J27.pin1

custom parts:
  IchigoJam T: IchigoJam T (IchigoJam means also strawberry jam) is a low-power, low-cost single board computer development platform. As "Kid's PC", it is developing for children's programming education. In this series, the BASIC language is activated just by turning on the power, and there is a feature that it can program immediately. Because it has I/O ports, it is easy to control electronic work, not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
  AE-DRV8835-S-1: DRV8835 stepping and DC motor control module.
  Power plug: 秋月電子通商 AE-DC-POWER-JACK-DIP(通販コードK-05148)とその互換品
  Terminal 2pin: 2-pin Terminal Block
  Akizuki slide switch IS-2235: Akizuki slide switch is-2235 (P-02627)
